# Fritzing sketch RadBit (saved by Fritzing 0.9.3b)

parts:
  IC1 = Teviso RD3024 [chip_label=IC]
  Part3 = SPI Non-Volatile FRAM 8KB
  Part1 = LightBlue Bean+
  C2 = Ceramic Capacitor [capacitance=10nF package="100 mil [THT, multilayer]"]

nets:
  N1: IC1.OUT, Part1.D0
  VCC: IC1.VCC, Part3.VCC, Part1.3.3V, C2.0
  GND: IC1.GND, Part3.GND, Part1.GND, C2.1
  N2: Part3.CS, Part1.D6/SS
  N3: Part3.MOSI, Part1.D7/MOSI
  N4: Part3.MISO, Part1.D8/MISO
  N5: Part3.SCK, Part1.D9/SCK

custom parts:
  Teviso RD3024: A low voltage solid state radiation sensor, in combination with high immunity to RF fields make it a good choice for new state-of-the-art designs of battery powered applications using WiFi, GSM and Bluetooth communication.
  SPI Non-Volatile FRAM 8KB: With our SPI FRAM breakout board you can add some FRAM storage to your next DIY project. FRAM allows for a lower power usage and a faster write performance. It's excellent for low-power or inconsistent-power datalogging or data buffering where you want to stream data fast while also keeping the data when there's no power. Unlike Flash or EEPROM there's no pages to worry about. Each byte can be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
  LightBlue Bean+: http://store.punchthrough.com/collections/all/products/lightblue-bean-plus
